// Logisim project tests.circ as structural Verilog
module Test_7400 (
);

  wire and_1_out, clock_1_out, n7400_1_p3, n7400_1_p6, n7400_1_p9, n7400_1_p12, nand_1_out, xnor_1_out,
       xnor_2_out, xnor_3_out, xnor_4_out;
  wire [1:0] counter_1_q;

  Clock clock_1 (.out(clock_1_out));
  Counter #(.width(2), .max('h3)) counter_1 (
    .count(1'b1), .Q(counter_1_q), .clk(clock_1_out));  // open: load, D, carry, clr
  // _7400 7400_1: pin names not known; wires that end beside it: counter_1_q[0], counter_1_q[1], n7400_1_p3, counter_1_q[0], counter_1_q[1], n7400_1_p6, counter_1_q[1], counter_1_q[0], n7400_1_p9, counter_1_q[1], counter_1_q[0], n7400_1_p12
  nand nand_1 (nand_1_out, counter_1_q[0], counter_1_q[1]);
  xnor xnor_1 (xnor_1_out, nand_1_out, n7400_1_p9);
  xnor xnor_2 (xnor_2_out, nand_1_out, n7400_1_p12);
  xnor xnor_3 (xnor_3_out, nand_1_out, n7400_1_p3);
  xnor xnor_4 (xnor_4_out, nand_1_out, n7400_1_p6);
  and and_1 (and_1_out, xnor_1_out, xnor_2_out, xnor_3_out, xnor_4_out);
  LED led_1 (.in(and_1_out));
endmodule

module Test_7402 (
);

  wire and_1_out, clock_1_out, n7402_1_p1, n7402_1_p4, n7402_1_p7, n7402_1_p10, nor_1_out, xnor_1_out,
       xnor_2_out, xnor_3_out, xnor_4_out;
  wire [1:0] counter_1_q;

  Clock clock_1 (.out(clock_1_out));
  Counter #(.width(2), .max('h3)) counter_1 (
    .count(1'b1), .Q(counter_1_q), .clk(clock_1_out));  // open: load, D, carry, clr
  // _7402 7402_1: pin names not known; wires that end beside it: n7402_1_p1, counter_1_q[0], counter_1_q[1], n7402_1_p4, counter_1_q[0], counter_1_q[1], n7402_1_p7, counter_1_q[1], counter_1_q[0], n7402_1_p10, counter_1_q[1], counter_1_q[0]
  nor nor_1 (nor_1_out, counter_1_q[0], counter_1_q[1]);
  xnor xnor_1 (xnor_1_out, nor_1_out, n7402_1_p7);
  xnor xnor_2 (xnor_2_out, nor_1_out, n7402_1_p10);
  xnor xnor_3 (xnor_3_out, nor_1_out, n7402_1_p1);
  xnor xnor_4 (xnor_4_out, nor_1_out, n7402_1_p4);
  LED led_1 (.in(and_1_out));
  and and_1 (and_1_out, xnor_1_out, xnor_2_out, xnor_3_out, xnor_4_out);
endmodule

module Test_7404 (
);

  wire and_1_out, clock_1_out, counter_1_q, n7404_1_p2, n7404_1_p4, n7404_1_p6, n7404_1_p8, n7404_1_p10,
       n7404_1_p12, not_1_out, xnor_1_out, xnor_2_out, xnor_3_out, xnor_4_out, xnor_5_out, xnor_6_out;

  Counter #(.width(1), .max('h1)) counter_1 (
    .count(1'b1), .Q(counter_1_q), .clk(clock_1_out));  // open: load, D, carry, clr
  Clock clock_1 (.out(clock_1_out));
  // _7404 7404_1: pin names not known; wires that end beside it: counter_1_q, n7404_1_p2, counter_1_q, n7404_1_p4, counter_1_q, n7404_1_p6, counter_1_q, n7404_1_p8, counter_1_q, n7404_1_p10, counter_1_q, n7404_1_p12
  not not_1 (not_1_out, counter_1_q);
  xnor xnor_1 (xnor_1_out, not_1_out, n7404_1_p8);
  xnor xnor_2 (xnor_2_out, not_1_out, n7404_1_p10);
  xnor xnor_3 (xnor_3_out, not_1_out, n7404_1_p12);
  xnor xnor_4 (xnor_4_out, not_1_out, n7404_1_p2);
  xnor xnor_5 (xnor_5_out, not_1_out, n7404_1_p4);
  xnor xnor_6 (xnor_6_out, not_1_out, n7404_1_p6);
  LED led_1 (.in(and_1_out));
  and and_1 (and_1_out, xnor_1_out, xnor_2_out, xnor_3_out, xnor_4_out, xnor_5_out, xnor_6_out);
endmodule

module Test_7408 (
);

  wire and_1_out, and_2_out, clock_1_out, n7408_1_p3, n7408_1_p6, n7408_1_p9, n7408_1_p12, xnor_1_out,
       xnor_2_out, xnor_3_out, xnor_4_out;
  wire [1:0] counter_1_q;

  Clock clock_1 (.out(clock_1_out));
  Counter #(.width(2), .max('h3)) counter_1 (
    .count(1'b1), .Q(counter_1_q), .clk(clock_1_out));  // open: load, D, carry, clr
  // _7408 7408_1: pin names not known; wires that end beside it: counter_1_q[0], counter_1_q[1], n7408_1_p3, counter_1_q[0], counter_1_q[1], n7408_1_p6, counter_1_q[1], counter_1_q[0], n7408_1_p9, counter_1_q[1], counter_1_q[0], n7408_1_p12
  and and_1 (and_1_out, counter_1_q[0], counter_1_q[1]);
  xnor xnor_1 (xnor_1_out, and_1_out, n7408_1_p9);
  xnor xnor_2 (xnor_2_out, and_1_out, n7408_1_p12);
  xnor xnor_3 (xnor_3_out, and_1_out, n7408_1_p3);
  xnor xnor_4 (xnor_4_out, and_1_out, n7408_1_p6);
  and and_2 (and_2_out, xnor_1_out, xnor_2_out, xnor_3_out, xnor_4_out);
  LED led_1 (.in(and_2_out));
endmodule

module Test_7410 (
);

  wire and_1_out, clock_1_out, n7410_1_p6, n7410_1_p8, n7410_1_p12, nand_1_out, xnor_1_out, xnor_2_out,
       xnor_3_out;
  wire [2:0] counter_1_q;

  Clock clock_1 (.out(clock_1_out));
  Counter #(.width(3), .max('h7)) counter_1 (
    .count(1'b1), .Q(counter_1_q), .clk(clock_1_out));  // open: load, D, carry, clr
  // _7410 7410_1: pin names not known; wires that end beside it: counter_1_q[0], counter_1_q[1], counter_1_q[0], counter_1_q[1], counter_1_q[2], n7410_1_p6, counter_1_q[2], n7410_1_p8, counter_1_q[2], counter_1_q[1], counter_1_q[0], n7410_1_p12
  nand nand_1 (nand_1_out, counter_1_q[0], counter_1_q[1], counter_1_q[2]);
  xnor xnor_1 (xnor_1_out, nand_1_out, n7410_1_p8);
  xnor xnor_2 (xnor_2_out, nand_1_out, n7410_1_p12);
  xnor xnor_3 (xnor_3_out, nand_1_out, n7410_1_p6);
  LED led_1 (.in(and_1_out));
  and and_1 (and_1_out, xnor_1_out, xnor_2_out, xnor_3_out);
endmodule

module Test_7411 (
);

  wire and_1_out, and_2_out, clock_1_out, n7411_1_p6, n7411_1_p8, n7411_1_p12, xnor_1_out, xnor_2_out,
       xnor_3_out;
  wire [2:0] counter_1_q;

  Clock clock_1 (.out(clock_1_out));
  Counter #(.width(3), .max('h7)) counter_1 (
    .count(1'b1), .Q(counter_1_q), .clk(clock_1_out));  // open: load, D, carry, clr
  // _7411 7411_1: pin names not known; wires that end beside it: counter_1_q[0], counter_1_q[1], counter_1_q[0], counter_1_q[1], counter_1_q[2], n7411_1_p6, counter_1_q[2], n7411_1_p8, counter_1_q[2], counter_1_q[1], counter_1_q[0], n7411_1_p12
  and and_1 (and_1_out, counter_1_q[0], counter_1_q[1], counter_1_q[2]);
  xnor xnor_1 (xnor_1_out, and_1_out, n7411_1_p8);
  xnor xnor_2 (xnor_2_out, and_1_out, n7411_1_p12);
  xnor xnor_3 (xnor_3_out, and_1_out, n7411_1_p6);
  and and_2 (and_2_out, xnor_1_out, xnor_2_out, xnor_3_out);
  LED led_1 (.in(and_2_out));
endmodule

module Test_7420 (
);

  wire and_1_out, clock_1_out, n7420_1_p5, n7420_1_p10, nand_1_out, xnor_1_out, xnor_2_out;
  wire [3:0] counter_1_q;

  Clock clock_1 (.out(clock_1_out));
  Counter #(.width(4), .max('hf)) counter_1 (
    .count(1'b1), .Q(counter_1_q), .clk(clock_1_out));  // open: load, D, carry, clr
  // _7420 7420_1: pin names not known; wires that end beside it: counter_1_q[0], counter_1_q[1], counter_1_q[2], counter_1_q[3], n7420_1_p5, counter_1_q[3], counter_1_q[2], counter_1_q[1], counter_1_q[0], n7420_1_p10
  nand nand_1 (nand_1_out, counter_1_q[0], counter_1_q[1], counter_1_q[2], counter_1_q[3]);
  xnor xnor_1 (xnor_1_out, nand_1_out, n7420_1_p10);
  xnor xnor_2 (xnor_2_out, nand_1_out, n7420_1_p5);
  and and_1 (and_1_out, xnor_1_out, xnor_2_out);
  LED led_1 (.in(and_1_out));
endmodule

module Test_7421 (
);

  wire and_1_out, and_2_out, clock_1_out, n7421_1_p5, n7421_1_p10, xnor_1_out, xnor_2_out;
  wire [3:0] counter_1_q;

  Clock clock_1 (.out(clock_1_out));
  Counter #(.width(4), .max('hf)) counter_1 (
    .count(1'b1), .Q(counter_1_q), .clk(clock_1_out));  // open: load, D, carry, clr
  // _7421 7421_1: pin names not known; wires that end beside it: counter_1_q[0], counter_1_q[1], counter_1_q[2], counter_1_q[3], n7421_1_p5, counter_1_q[3], counter_1_q[2], counter_1_q[1], counter_1_q[0], n7421_1_p10
  and and_1 (and_1_out, counter_1_q[0], counter_1_q[1], counter_1_q[2], counter_1_q[3]);
  xnor xnor_1 (xnor_1_out, and_1_out, n7421_1_p10);
  xnor xnor_2 (xnor_2_out, and_1_out, n7421_1_p5);
  and and_2 (and_2_out, xnor_1_out, xnor_2_out);
  LED led_1 (.in(and_2_out));
endmodule

module Test_7425 (
);

  wire and_1_out, clock_1_out, n7425_1_p5, n7425_1_p10, nor_1_out, xnor_1_out, xnor_2_out;
  wire [3:0] counter_1_q;

  Clock clock_1 (.out(clock_1_out));
  Counter #(.width(4), .max('hf)) counter_1 (
    .count(1'b1), .Q(counter_1_q), .clk(clock_1_out));  // open: load, D, carry, clr
  // _7425 7425_1: pin names not known; wires that end beside it: counter_1_q[0], counter_1_q[1], counter_1_q[2], counter_1_q[3], n7425_1_p5, counter_1_q[3], counter_1_q[2], counter_1_q[1], counter_1_q[0], n7425_1_p10
  nor nor_1 (nor_1_out, counter_1_q[0], counter_1_q[1], counter_1_q[2], counter_1_q[3]);
  xnor xnor_1 (xnor_1_out, nor_1_out, n7425_1_p10);
  xnor xnor_2 (xnor_2_out, nor_1_out, n7425_1_p5);
  LED led_1 (.in(and_1_out));
  and and_1 (and_1_out, xnor_1_out, xnor_2_out);
endmodule

module Test_7427 (
);

  wire and_1_out, clock_1_out, n7427_1_p6, n7427_1_p8, n7427_1_p12, nor_1_out, xnor_1_out, xnor_2_out,
       xnor_3_out;
  wire [2:0] counter_1_q;

  Clock clock_1 (.out(clock_1_out));
  Counter #(.width(3), .max('h7)) counter_1 (
    .count(1'b1), .Q(counter_1_q), .clk(clock_1_out));  // open: load, D, carry, clr
  // _7427 7427_1: pin names not known; wires that end beside it: counter_1_q[0], counter_1_q[1], counter_1_q[0], counter_1_q[1], counter_1_q[2], n7427_1_p6, counter_1_q[2], n7427_1_p8, counter_1_q[2], counter_1_q[1], counter_1_q[0], n7427_1_p12
  nor nor_1 (nor_1_out, counter_1_q[0], counter_1_q[1], counter_1_q[2]);
  xnor xnor_1 (xnor_1_out, nor_1_out, n7427_1_p8);
  xnor xnor_2 (xnor_2_out, nor_1_out, n7427_1_p12);
  xnor xnor_3 (xnor_3_out, nor_1_out, n7427_1_p6);
  LED led_1 (.in(and_1_out));
  and and_1 (and_1_out, xnor_1_out, xnor_2_out, xnor_3_out);
endmodule

module Test_7432 (
);

  wire and_1_out, clock_1_out, n7432_1_p3, n7432_1_p6, n7432_1_p9, n7432_1_p12, or_1_out, xnor_1_out,
       xnor_2_out, xnor_3_out, xnor_4_out;
  wire [1:0] counter_1_q;

  Clock clock_1 (.out(clock_1_out));
  Counter #(.width(2), .max('h3)) counter_1 (
    .count(1'b1), .Q(counter_1_q), .clk(clock_1_out));  // open: load, D, carry, clr
  // _7432 7432_1: pin names not known; wires that end beside it: counter_1_q[0], counter_1_q[1], n7432_1_p3, counter_1_q[0], counter_1_q[1], n7432_1_p6, counter_1_q[1], counter_1_q[0], n7432_1_p9, counter_1_q[1], counter_1_q[0], n7432_1_p12
  or or_1 (or_1_out, counter_1_q[0], counter_1_q[1]);
  xnor xnor_1 (xnor_1_out, or_1_out, n7432_1_p9);
  xnor xnor_2 (xnor_2_out, or_1_out, n7432_1_p12);
  xnor xnor_3 (xnor_3_out, or_1_out, n7432_1_p3);
  xnor xnor_4 (xnor_4_out, or_1_out, n7432_1_p6);
  LED led_1 (.in(and_1_out));
  and and_1 (and_1_out, xnor_1_out, xnor_2_out, xnor_3_out, xnor_4_out);
endmodule

module Test_4786 (
);

  wire and_1_out, clock_1_out, n7486_1_p3, n7486_1_p6, n7486_1_p9, n7486_1_p12, xnor_1_out, xnor_2_out,
       xnor_3_out, xnor_4_out, xor_1_out;
  wire [1:0] counter_1_q;

  Clock clock_1 (.out(clock_1_out));
  Counter #(.width(2), .max('h3)) counter_1 (
    .count(1'b1), .Q(counter_1_q), .clk(clock_1_out));  // open: load, D, carry, clr
  // _7486 7486_1: pin names not known; wires that end beside it: counter_1_q[0], counter_1_q[1], n7486_1_p3, counter_1_q[0], counter_1_q[1], n7486_1_p6, counter_1_q[1], counter_1_q[0], n7486_1_p9, counter_1_q[1], counter_1_q[0], n7486_1_p12
  xor xor_1 (xor_1_out, counter_1_q[0], counter_1_q[1]);
  xnor xnor_1 (xnor_1_out, xor_1_out, n7486_1_p9);
  xnor xnor_2 (xnor_2_out, xor_1_out, n7486_1_p12);
  xnor xnor_3 (xnor_3_out, xor_1_out, n7486_1_p3);
  xnor xnor_4 (xnor_4_out, xor_1_out, n7486_1_p6);
  LED led_1 (.in(and_1_out));
  and and_1 (and_1_out, xnor_1_out, xnor_2_out, xnor_3_out, xnor_4_out);
endmodule

module Test_744075 (
);

  wire and_1_out, clock_1_out, n744075_1_p6, n744075_1_p10, n744075_1_p11, or_1_out, xnor_1_out, xnor_2_out,
       xnor_3_out;
  wire [2:0] counter_1_q;

  Clock clock_1 (.out(clock_1_out));
  Counter #(.width(3), .max('h7)) counter_1 (
    .count(1'b1), .Q(counter_1_q), .clk(clock_1_out));  // open: load, D, carry, clr
  // _744075 744075_1: pin names not known; wires that end beside it: counter_1_q[0], counter_1_q[1], counter_1_q[0], counter_1_q[1], counter_1_q[2], n744075_1_p6, counter_1_q[2], counter_1_q[1], counter_1_q[0], n744075_1_p10, n744075_1_p11, counter_1_q[2]
  or or_1 (or_1_out, counter_1_q[0], counter_1_q[1], counter_1_q[2]);
  xnor xnor_1 (xnor_1_out, or_1_out, n744075_1_p10);
  xnor xnor_2 (xnor_2_out, or_1_out, n744075_1_p11);
  xnor xnor_3 (xnor_3_out, or_1_out, n744075_1_p6);
  LED led_1 (.in(and_1_out));
  and and_1 (and_1_out, xnor_1_out, xnor_2_out, xnor_3_out);
endmodule

module Test_744511 (
  input  D3,
  input  D2,
  input  D1,
  input  D0,
  input  Load,
  input  Lamp_Test,
  input  Blank
);

  wire n744511_1_p8, n744511_1_p9, n744511_1_p10, n744511_1_p11, n744511_1_p12, n744511_1_p13, n744511_1_p14;

  // _744511 744511_1: pin names not known; wires that end beside it: D1, D2, Lamp_Test, Blank, Load, D3, D0, n744511_1_p8, n744511_1_p9, n744511_1_p10, n744511_1_p11, n744511_1_p12, n744511_1_p13, n744511_1_p14
  _7_Segment_Display u_7_segment_display_1 (
    .g(n744511_1_p9), .f(n744511_1_p8), .a(n744511_1_p10), .b(n744511_1_p11), .e(n744511_1_p14),
    .d(n744511_1_p13), .c(n744511_1_p12));  // open: dp
endmodule
